// Logisim project Dragon_5.circ as structural Verilog
module ALU (
  input  [3:0] ALU_OP_IN,
  input  [15:0] ALU_A_IN,
  input  [15:0] ALU_B_IN,
  output [15:0] ALU_RES_OUT,
  output [3:0] ALU_FLAG_OUT
);

  Multiplexer #(.select(4), .width(16)) multiplexer_1 (
    .out(ALU_RES_OUT), .sel(ALU_OP_IN));  // open: in0, in1, in2, in3, in4, in5, in6, in7, in8, in9, in10, in11, in12, in13, in14, in15
endmodule
